// Logisim project modular_adder_subtractor_circuit.circ as structural Verilog: 4 circuits, main circuit main
module main (
  input  s,
  input  x3,
  input  y3,
  input  x2,
  input  y2,
  input  x1,
  input  y1,
  input  x0,
  input  y0
);

  wire black_node_1_gigj, black_node_1_pipj, black_node_2_gigj, black_node_3_gigj, black_node_4_gigj,
       black_node_4_pipj, black_node_5_gigj, black_node_5_pipj, black_node_6_gigj, black_node_7_gigj,
       black_node_8_gigj, black_node_8_pipj, hal_1_ai, hal_1_bj, hal_1_not_ai, hal_1_not_bj, hal_2_ai,
       hal_2_bj, hal_2_not_ai, hal_2_not_bj, hal_3_ai, hal_3_bj, hal_3_not_ai, hal_3_not_bj, hal_4_ai,
       hal_4_bj, hal_4_not_ai, hal_4_not_bj, multiplexer_1_out, multiplexer_2_out, multiplexer_3_out,
       multiplexer_4_out, multiplexer_5_out, multiplexer_6_out, multiplexer_7_out, multiplexer_8_out,
       precomputation_1_gi, precomputation_1_hi, precomputation_1_pi, precomputation_2_gi,
       precomputation_2_hi, precomputation_2_pi, precomputation_3_gi, precomputation_3_hi,
       precomputation_3_pi, precomputation_4_gi, precomputation_4_hi, precomputation_4_pi,
       precomputation_5_gi, precomputation_5_hi, precomputation_5_pi, precomputation_6_gi,
       precomputation_6_hi, precomputation_6_pi, precomputation_7_gi, precomputation_7_hi,
       precomputation_7_pi, precomputation_8_gi, precomputation_8_hi, precomputation_8_pi, xor_1_out,
       xor_2_out, xor_3_out, xor_4_out, xor_5_out, xor_6_out, xor_7_out, xor_8_out, xor_9_out, xor_10_out;

  Multiplexer multiplexer_1 (.in0(hal_1_not_bj), .in1(hal_1_bj), .out(multiplexer_1_out), .sel(s));
  xor xor_1 (xor_1_out, y3, s);
  HAL hal_1 (.yi_xor_s(xor_1_out), .xi(x3), .Ai(hal_1_ai), .NOT_Ai(hal_1_not_ai), .Bj(hal_1_bj), .NOT_Bj(hal_1_not_bj));
  Multiplexer multiplexer_2 (.in0(hal_1_not_ai), .in1(hal_1_ai), .out(multiplexer_2_out), .sel(s));
  Multiplexer multiplexer_3 (.in0(hal_2_not_bj), .in1(hal_2_bj), .out(multiplexer_3_out), .sel(s));
  precomputation precomputation_1 (
    .ai(multiplexer_2_out), .bi(multiplexer_3_out), .Hi(precomputation_1_hi), .Gi(precomputation_1_gi),
    .Pi(precomputation_1_pi));
  black_node black_node_1 (
    .Gi(precomputation_1_gi), .Gj(precomputation_2_gi), .Pi(precomputation_1_pi), .Pj(precomputation_2_pi),
    .GiGj(black_node_1_gigj), .PiPj(black_node_1_pipj));
  black_node black_node_2 (
    .Gi(black_node_1_gigj), .Gj(black_node_4_gigj), .Pi(black_node_1_pipj), .Pj(black_node_4_pipj),
    .GiGj(black_node_2_gigj));  // open: PiPj
  xor xor_2 (xor_2_out, precomputation_1_hi, black_node_3_gigj);
  xor xor_3 (xor_3_out, y2, s);
  HAL hal_2 (.yi_xor_s(xor_3_out), .xi(x2), .Ai(hal_2_ai), .NOT_Ai(hal_2_not_ai), .Bj(hal_2_bj), .NOT_Bj(hal_2_not_bj));
  Multiplexer multiplexer_4 (.in0(hal_2_not_ai), .in1(hal_2_ai), .out(multiplexer_4_out), .sel(s));
  xor xor_4 (xor_4_out, precomputation_2_hi, black_node_4_gigj);
  Multiplexer multiplexer_5 (.in0(hal_3_not_bj), .in1(hal_3_bj), .out(multiplexer_5_out), .sel(s));
  precomputation precomputation_2 (
    .ai(multiplexer_4_out), .bi(multiplexer_5_out), .Hi(precomputation_2_hi), .Gi(precomputation_2_gi),
    .Pi(precomputation_2_pi));
  black_node black_node_3 (
    .Gi(precomputation_2_gi), .Gj(black_node_4_gigj), .Pi(precomputation_2_pi), .Pj(black_node_4_pipj),
    .GiGj(black_node_3_gigj));  // open: PiPj
  xor xor_5 (xor_5_out, y1, s);
  HAL hal_3 (.yi_xor_s(xor_5_out), .xi(x1), .Ai(hal_3_ai), .NOT_Ai(hal_3_not_ai), .Bj(hal_3_bj), .NOT_Bj(hal_3_not_bj));
  Multiplexer multiplexer_6 (.in0(hal_3_not_ai), .in1(hal_3_ai), .out(multiplexer_6_out), .sel(s));
  precomputation precomputation_3 (
    .ai(multiplexer_6_out), .bi(multiplexer_7_out), .Hi(precomputation_3_hi), .Gi(precomputation_3_gi),
    .Pi(precomputation_3_pi));
  xor xor_6 (xor_6_out, precomputation_3_hi, precomputation_4_gi);
  HAL hal_4 (.yi_xor_s(xor_7_out), .xi(x0), .Ai(hal_4_ai), .NOT_Ai(hal_4_not_ai), .Bj(hal_4_bj), .NOT_Bj(hal_4_not_bj));
  Multiplexer multiplexer_7 (.in0(hal_4_not_bj), .in1(hal_4_bj), .out(multiplexer_7_out), .sel(s));
  black_node black_node_4 (
    .Gi(precomputation_3_gi), .Gj(precomputation_4_gi), .Pi(precomputation_3_pi), .Pj(precomputation_4_pi),
    .GiGj(black_node_4_gigj), .PiPj(black_node_4_pipj));
  xor xor_7 (xor_7_out, y0, s);
  Multiplexer multiplexer_8 (.in0(hal_4_not_ai), .in1(hal_4_ai), .out(multiplexer_8_out), .sel(s));
  precomputation precomputation_4 (
    .ai(multiplexer_8_out), .bi(1'b1), .Hi(precomputation_4_hi), .Gi(precomputation_4_gi),
    .Pi(precomputation_4_pi));
  precomputation precomputation_5 (
    .ai(hal_1_ai), .bi(hal_2_bj), .Hi(precomputation_5_hi), .Gi(precomputation_5_gi), .Pi(precomputation_5_pi));
  xor xor_8 (xor_8_out, precomputation_5_hi, black_node_7_gigj);
  black_node black_node_5 (
    .Gi(precomputation_5_gi), .Gj(precomputation_6_gi), .Pi(precomputation_5_pi), .Pj(precomputation_6_pi),
    .GiGj(black_node_5_gigj), .PiPj(black_node_5_pipj));
  black_node black_node_6 (
    .Gi(black_node_5_gigj), .Gj(black_node_8_gigj), .Pi(black_node_5_pipj), .Pj(black_node_8_pipj),
    .GiGj(black_node_6_gigj));  // open: PiPj
  precomputation precomputation_6 (
    .ai(hal_2_ai), .bi(hal_3_bj), .Hi(precomputation_6_hi), .Gi(precomputation_6_gi), .Pi(precomputation_6_pi));
  black_node black_node_7 (
    .Gi(precomputation_6_gi), .Gj(black_node_8_gigj), .Pi(precomputation_6_pi), .Pj(black_node_8_pipj),
    .GiGj(black_node_7_gigj));  // open: PiPj
  xor xor_9 (xor_9_out, precomputation_6_hi, black_node_8_gigj);
  precomputation precomputation_7 (
    .ai(hal_3_ai), .bi(hal_4_bj), .Hi(precomputation_7_hi), .Gi(precomputation_7_gi), .Pi(precomputation_7_pi));
  black_node black_node_8 (
    .Gi(precomputation_7_gi), .Gj(precomputation_8_gi), .Pi(precomputation_7_pi), .Pj(precomputation_8_pi),
    .GiGj(black_node_8_gigj), .PiPj(black_node_8_pipj));
  xor xor_10 (xor_10_out, precomputation_7_hi, precomputation_8_gi);
  precomputation precomputation_8 (
    .ai(s), .bi(hal_4_ai), .Hi(precomputation_8_hi), .Gi(precomputation_8_gi), .Pi(precomputation_8_pi));
endmodule

module HAL (
  input  yi_xor_s,
  input  xi,
  output Ai,
  output NOT_Ai,
  output Bj,
  output NOT_Bj
);

  xor xor_1 (Ai, yi_xor_s, xi);
  not not_1 (NOT_Ai, Ai);
  and and_1 (Bj, yi_xor_s, xi);
  or or_1 (NOT_Bj, xi, yi_xor_s);
endmodule

module precomputation (
  input  ai,
  input  bi,
  output Hi,
  output Gi,
  output Pi
);

  xor xor_1 (Hi, ai, bi);
  and and_1 (Gi, ai, bi);
  or or_1 (Pi, ai, bi);
endmodule

module black_node (
  input  Gi,
  input  Gj,
  input  Pi,
  input  Pj,
  output PiPj,
  output GiGj
);

  wire and_1_out;

  and and_1 (and_1_out, Gj, Pi);
  or or_1 (GiGj, Gi, and_1_out);
  and and_2 (PiPj, Pi, Pj);

  // Notes on the sheet:
  //   j=i-1
endmodule
